# Fritzing sketch LED board (saved by Fritzing 0.9.9b)
circuit board: 4.38729cm x 2.06208cm
breadboards: 1

parts:
  220 = Resistor [tolerance=±5% power=0.25 resistance=220 package=THT]
  220_2 = Resistor [tolerance=±5% power=0.25 resistance=220 package=THT]
  3_is_GND = JST-VHR-3N [part_number=JST-VHR-3N package=THT]
  Green = LED - 5mm [color="Green (570nm)" current=0.030 package="5 mm [THT]"]
  Red = LED - 5mm [color="Red (633nm)" current=0.030 package="5 mm [THT]"]

nets:
  N1: 220.Pin_0, Green.anode
  N2: 220.Pin_1, 3_is_GND.pin2
  N3: 220_2.Pin_0, Red.anode
  N4: 220_2.Pin_1, 3_is_GND.pin1
  N5: 3_is_GND.pin3, Green.cathode, Red.cathode
