# Fritzing sketch Main Board (saved by Fritzing 0.9.9b)
breadboards: 1

parts:
  Part1 = ESP-WROOM-32 [ESP-32S] Module [part_number=ESP-WROOM-32]
  Battery_[]MiAh = LIPO-2000mAh [package=lipo-2000]  # not connected
  SDP_33 = SDP33 [chip_label=SDP33 package="DIP (Dual Inline) [THT]"]  # not connected
  Part2 = InvenSense MPU6050
  To_LED_Board = JST-B3P-VH [part_number=JST-B3P-VH package=THT]

nets:
  N1: Part1.GND#0, Part2.GND
  3V3: Part1.3V3, Part2.VCC
  N2: Part1.GND#51, To_LED_Board.pin3

notes:
  Need to find/make part for 4056-c USBC battery regulator for charging
  1 is RED 2 is GREEN 3 is GND. resistors on led board. Can power each light independantly

custom parts:
  ESP-WROOM-32 [ESP-32S] Module: Espressif ESP-WROOM-32 WiFi/Bluetooth LE microcontroller module also known as the Ai-Thinker ESP-32S module with similar formfactor. The ESP32 is a microcontroller chip with WiFi and BLE capabilities. The chip is developed by Espressif and is the successor to the popular ESP8266 WiFi module.
  SDP33: A DIP stand-in part for whatever IC you want. With 16 pins on a 300mil dual inline package (DIP) footprint.
