# Fritzing sketch button board (saved by Fritzing 0.9.9b)
circuit board: 3.42531cm x 3.01115cm
breadboards: 1

parts:
  S1 = Pushbutton [package="[THT]"]
  S2 = Pushbutton [package="[THT]"]
  10k = Resistor [tolerance=±5% power=0.25 resistance=10k package=THT]
  10k_2 = Resistor [tolerance=±5% power=0.25 resistance=10k package=THT]
  To_Main_Board_2/4_=_GND = Header 4 [package=1x04-1mm-ra]

nets:
  N1: S1.Pin_2, 10k.Pin_0
  N2: S1.Pin_3, S1.Pin_4, To_Main_Board_2/4_=_GND.1
  N3: S2.Pin_1, S2.Pin_2, 10k_2.Pin_0
  N4: S2.Pin_3, To_Main_Board_2/4_=_GND.3
  N5: 10k.Pin_1, To_Main_Board_2/4_=_GND.2
  N6: 10k_2.Pin_1, To_Main_Board_2/4_=_GND.4
