# Fritzing sketch gyroBoard(WIRED) (saved by Fritzing 0.9.9b)
circuit board: 4.29804cm x 3.07509cm
breadboards: 1

parts:
  MPU_6050 = InvenSense MPU6050
  VCC_GND_SCL_SDA = Camdenboss CTB0158-4 [part_number=CTB0158-4 package=THT]

nets:
  N1: MPU_6050.VCC, VCC_GND_SCL_SDA.pin1
  N2: MPU_6050.GND, VCC_GND_SCL_SDA.pin2
  N3: MPU_6050.SCL, VCC_GND_SCL_SDA.pin3
  N4: MPU_6050.SDA, VCC_GND_SCL_SDA.pin4

notes:
  Need part to make into USB-C connector
  need a part for the battery charger (4056-c) and transmitter if going wireless
