# Fritzing sketch pressureSensor1 (saved by Fritzing 0.9.9b)
circuit board: 2.58211cm x 3.71578cm
breadboards: 1

parts:
  GND_3_2_1 = Camdenboss CTB0158-4 [part_number=CTB0158-4 package=THT]
  Index = female pin header, 2 pins [form="♀ (female)"]
  Middle = female pin header, 2 pins [form="♀ (female)"]
  Ring = female pin header, 2 pins [form="♀ (female)"]
  R2_1k = Resistor [tolerance=±5% power=0.25 resistance=1k package=THT]
  R1_1k = Resistor [tolerance=±5% power=0.25 resistance=1k package=THT]
  R3_1k = Resistor [tolerance=±5% power=0.25 resistance=1k package=THT]

nets:
  N1: GND_3_2_1.pin1, Index.pin1
  N2: GND_3_2_1.pin2, Middle.pin1
  N3: GND_3_2_1.pin3, Ring.pin1
  N4: GND_3_2_1.pin4, R2_1k.Pin_1, R1_1k.Pin_1, R3_1k.Pin_1
  N5: Index.pin2, R1_1k.Pin_0
  N6: Middle.pin2, R2_1k.Pin_0
  N7: Ring.pin2, R3_1k.Pin_0
