# Fritzing sketch pressureSensor2 (saved by Fritzing 0.9.9b)
breadboards: 1

parts:
  J1 = Basic Force Sensing Resistor (FSR) [package=THT]
  J2 = Basic Force Sensing Resistor (FSR) [package=THT]
  J3 = Basic Force Sensing Resistor (FSR) [package=THT]
  J4 = female pin header, 2 pins [form="♀ (female)"]
  J5 = female pin header, 2 pins [form="♀ (female)"]
  J6 = female pin header, 2 pins [form="♀ (female)"]

nets:
  N1: J1.pin_0, J4.pin2
  N2: J1.pin_1, J4.pin1
  N3: J2.pin_0, J5.pin2
  N4: J2.pin_1, J5.pin1
  N5: J3.pin_0, J6.pin2
  N6: J3.pin_1, J6.pin1
